// Logisim project Beta CPU - DSP.circ as structural Verilog
module MSB_ALU (
  input  [2:0] in_1,
  input  in_2,
  input  Cin,
  input  A,
  input  B,
  input  CMPLT___0,
  output out_7,
  output CMPEQ_OUT,
  output CMPLT_OUT
);

  wire AND_out, multiplexer_1_out, not_1_out, OR_out, XOR_out;

  not not_1 (not_1_out, B);
  Multiplexer #(.enable("false")) multiplexer_1 (.in0(B), .in1(not_1_out), .out(multiplexer_1_out), .sel(in_2));
  Adder #(.width(1)) adder_1 (.a(A), .b(multiplexer_1_out), .out(CMPLT_OUT), .cin(Cin));  // open: cout
  and AND (AND_out, A, multiplexer_1_out);
  or OR (OR_out, A, multiplexer_1_out);
  xor XOR (XOR_out, A, multiplexer_1_out);
  not not_2 (CMPEQ_OUT, XOR_out);
  Multiplexer #(.select(3), .enable("false")) multiplexer_2 (
    .in0(AND_out), .in1(OR_out), .in2(XOR_out), .in3(CMPEQ_OUT), .in4(CMPLT_OUT), .in5(CMPLT___0),
    .in6(CMPLT___0), .in7(CMPLT___0), .out(out_7), .sel(in_1));

  // Notes on the sheet:
  //   B'
  //   XNOR
  //   To AND Gate in Bit ALU
  //   To LSB ALU
endmodule

module LSB_ALU (
  input  [2:0] in_1,
  input  in_2,
  input  CMPLT_IN,
  input  Cin,
  input  From_Bit_ALU_30,
  input  in_6,
  input  in_7,
  output out_8,
  output out_9,
  output Cout
);

  wire adder_1_out, AND_out, multiplexer_1_out, not_1_out, not_2_out, or_2_out, OR_out, XOR_out;

  not not_1 (not_1_out, in_7);
  Multiplexer #(.enable("false")) multiplexer_1 (.in0(in_7), .in1(not_1_out), .out(multiplexer_1_out), .sel(in_2));
  Adder #(.width(1)) adder_1 (.a(in_6), .b(multiplexer_1_out), .out(adder_1_out), .cin(Cin), .cout(Cout));
  and AND (AND_out, in_6, multiplexer_1_out);
  or OR (OR_out, in_6, multiplexer_1_out);
  xor XOR (XOR_out, in_6, multiplexer_1_out);
  not not_2 (not_2_out, XOR_out);
  and and_2 (out_9, From_Bit_ALU_30, not_2_out);
  or or_2 (or_2_out, out_9, CMPLT_IN);
  Multiplexer #(.select(3), .enable("false")) multiplexer_2 (
    .in0(AND_out), .in1(OR_out), .in2(XOR_out), .in3(not_2_out), .in4(adder_1_out), .in5(out_9),
    .in6(or_2_out), .in7(CMPLT_IN), .out(out_8), .sel(in_1));

  // Notes on the sheet:
  //   B'
  //   From MSB ALU
  //   To 30th 1-Bit ALU
  //   XNOR
  //   CMPEQ IN
  //   CMPEQ
  //   CMPLEQ
  //   Zero for Branch instr
endmodule

module Bit_ALU (
  input  [2:0] in_1,
  input  in_2,
  input  Cin,
  input  CMPEQ_IN,
  input  A,
  input  B,
  input  CMPLT___0,
  output out_8,
  output Cout,
  output To_next_Bit_ALU
);

  wire adder_1_out, AND_out, multiplexer_1_out, not_1_out, not_2_out, OR_out, XOR_out;

  not not_1 (not_1_out, B);
  Multiplexer #(.enable("false")) multiplexer_1 (.in0(B), .in1(not_1_out), .out(multiplexer_1_out), .sel(in_2));
  Adder #(.width(1)) adder_1 (.a(A), .b(multiplexer_1_out), .out(adder_1_out), .cin(Cin), .cout(Cout));
  and AND (AND_out, A, multiplexer_1_out);
  or OR (OR_out, A, multiplexer_1_out);
  xor XOR (XOR_out, A, multiplexer_1_out);
  not not_2 (not_2_out, XOR_out);
  and and_2 (To_next_Bit_ALU, CMPEQ_IN, not_2_out);
  Multiplexer #(.select(3), .enable("false")) multiplexer_2 (
    .in0(AND_out), .in1(OR_out), .in2(XOR_out), .in3(not_2_out), .in4(adder_1_out), .in5(CMPLT___0),
    .in6(CMPLT___0), .in7(CMPLT___0), .out(out_8), .sel(in_1));

  // Notes on the sheet:
  //   B'
  //   XNOR
  //   From previous Bit ALU
  //   CMPEQ OUT
  //   CMPLE = 0
  //   CMPEQ = 0
endmodule

module Final_ALU32 (
  input  [31:0] in_1,
  input  Subtract_Ctrl,
  input  [2:0] in_3,
  input  [31:0] in_4,
  output [31:0] out_5
);

  wire bit_alu_1_cout, bit_alu_1_to_next_bit_alu, bit_alu_2_cout, bit_alu_2_to_next_bit_alu, bit_alu_3_cout,
       bit_alu_3_to_next_bit_alu, bit_alu_4_cout, bit_alu_4_to_next_bit_alu, bit_alu_5_cout,
       bit_alu_5_to_next_bit_alu, bit_alu_6_cout, bit_alu_6_to_next_bit_alu, bit_alu_7_cout,
       bit_alu_7_to_next_bit_alu, bit_alu_8_cout, bit_alu_8_to_next_bit_alu, bit_alu_9_cout,
       bit_alu_9_to_next_bit_alu, bit_alu_10_cout, bit_alu_10_to_next_bit_alu, bit_alu_11_cout,
       bit_alu_11_to_next_bit_alu, bit_alu_12_cout, bit_alu_12_to_next_bit_alu, bit_alu_13_cout,
       bit_alu_13_to_next_bit_alu, bit_alu_14_cout, bit_alu_14_to_next_bit_alu, bit_alu_15_cout,
       bit_alu_15_to_next_bit_alu, bit_alu_16_cout, bit_alu_16_to_next_bit_alu, bit_alu_17_cout,
       bit_alu_17_to_next_bit_alu, bit_alu_18_cout, bit_alu_18_to_next_bit_alu, bit_alu_19_cout,
       bit_alu_19_to_next_bit_alu, bit_alu_20_cout, bit_alu_20_to_next_bit_alu, bit_alu_21_cout,
       bit_alu_21_to_next_bit_alu, bit_alu_22_cout, bit_alu_22_to_next_bit_alu, bit_alu_23_cout,
       bit_alu_23_to_next_bit_alu, bit_alu_24_cout, bit_alu_24_to_next_bit_alu, bit_alu_25_cout,
       bit_alu_25_to_next_bit_alu, bit_alu_26_cout, bit_alu_26_to_next_bit_alu, bit_alu_27_cout,
       bit_alu_27_to_next_bit_alu, bit_alu_28_cout, bit_alu_28_to_next_bit_alu, bit_alu_29_cout,
       bit_alu_29_to_next_bit_alu, bit_alu_30_cout, bit_alu_30_to_next_bit_alu, lsb_alu_1_cout,
       lsb_alu_1_out_9, msb_alu_1_cmpeq_out, msb_alu_1_cmplt_out;

  Bit_ALU bit_alu_1 (
    .in_1(in_3), .A(in_1[30]), .B(in_4[30]), .out_8(out_5[30]), .in_2(Subtract_Ctrl), .Cin(bit_alu_2_cout),
    .CMPEQ_IN(msb_alu_1_cmpeq_out), .Cout(bit_alu_1_cout), .To_next_Bit_ALU(bit_alu_1_to_next_bit_alu),
    .CMPLT___0(1'b0));
  Bit_ALU bit_alu_2 (
    .in_1(in_3), .A(in_1[29]), .B(in_4[29]), .out_8(out_5[29]), .in_2(Subtract_Ctrl), .Cin(bit_alu_3_cout),
    .CMPEQ_IN(bit_alu_1_to_next_bit_alu), .Cout(bit_alu_2_cout), .To_next_Bit_ALU(bit_alu_2_to_next_bit_alu),
    .CMPLT___0(1'b0));
  Bit_ALU bit_alu_3 (
    .in_1(in_3), .A(in_1[28]), .B(in_4[28]), .out_8(out_5[28]), .in_2(Subtract_Ctrl), .Cin(bit_alu_4_cout),
    .CMPEQ_IN(bit_alu_2_to_next_bit_alu), .Cout(bit_alu_3_cout), .To_next_Bit_ALU(bit_alu_3_to_next_bit_alu),
    .CMPLT___0(1'b0));
  Bit_ALU bit_alu_4 (
    .in_1(in_3), .A(in_1[27]), .B(in_4[27]), .out_8(out_5[27]), .in_2(Subtract_Ctrl), .Cin(bit_alu_5_cout),
    .CMPEQ_IN(bit_alu_3_to_next_bit_alu), .Cout(bit_alu_4_cout), .To_next_Bit_ALU(bit_alu_4_to_next_bit_alu),
    .CMPLT___0(1'b0));
  Bit_ALU bit_alu_5 (
    .in_1(in_3), .A(in_1[26]), .B(in_4[26]), .out_8(out_5[26]), .in_2(Subtract_Ctrl), .Cin(bit_alu_6_cout),
    .CMPEQ_IN(bit_alu_4_to_next_bit_alu), .Cout(bit_alu_5_cout), .To_next_Bit_ALU(bit_alu_5_to_next_bit_alu),
    .CMPLT___0(1'b0));
  Bit_ALU bit_alu_6 (
    .in_1(in_3), .A(in_1[25]), .B(in_4[25]), .out_8(out_5[25]), .in_2(Subtract_Ctrl), .Cin(bit_alu_7_cout),
    .CMPEQ_IN(bit_alu_5_to_next_bit_alu), .Cout(bit_alu_6_cout), .To_next_Bit_ALU(bit_alu_6_to_next_bit_alu),
    .CMPLT___0(1'b0));
  Bit_ALU bit_alu_7 (
    .in_1(in_3), .A(in_1[24]), .B(in_4[24]), .out_8(out_5[24]), .in_2(Subtract_Ctrl), .Cin(bit_alu_8_cout),
    .CMPEQ_IN(bit_alu_6_to_next_bit_alu), .Cout(bit_alu_7_cout), .To_next_Bit_ALU(bit_alu_7_to_next_bit_alu),
    .CMPLT___0(1'b0));
  Bit_ALU bit_alu_8 (
    .in_1(in_3), .A(in_1[23]), .B(in_4[23]), .out_8(out_5[23]), .in_2(Subtract_Ctrl), .Cin(bit_alu_9_cout),
    .CMPEQ_IN(bit_alu_7_to_next_bit_alu), .Cout(bit_alu_8_cout), .To_next_Bit_ALU(bit_alu_8_to_next_bit_alu),
    .CMPLT___0(1'b0));
  Bit_ALU bit_alu_9 (
    .in_1(in_3), .A(in_1[22]), .B(in_4[22]), .out_8(out_5[22]), .in_2(Subtract_Ctrl), .Cin(bit_alu_10_cout),
    .CMPEQ_IN(bit_alu_8_to_next_bit_alu), .Cout(bit_alu_9_cout), .To_next_Bit_ALU(bit_alu_9_to_next_bit_alu),
    .CMPLT___0(1'b0));
  Bit_ALU bit_alu_10 (
    .in_1(in_3), .A(in_1[21]), .B(in_4[21]), .out_8(out_5[21]), .in_2(Subtract_Ctrl), .Cin(bit_alu_11_cout),
    .CMPEQ_IN(bit_alu_9_to_next_bit_alu), .Cout(bit_alu_10_cout),
    .To_next_Bit_ALU(bit_alu_10_to_next_bit_alu), .CMPLT___0(1'b0));
  Bit_ALU bit_alu_11 (
    .in_1(in_3), .A(in_1[20]), .B(in_4[20]), .out_8(out_5[20]), .in_2(Subtract_Ctrl), .Cin(bit_alu_12_cout),
    .CMPEQ_IN(bit_alu_10_to_next_bit_alu), .Cout(bit_alu_11_cout),
    .To_next_Bit_ALU(bit_alu_11_to_next_bit_alu), .CMPLT___0(1'b0));
  Bit_ALU bit_alu_12 (
    .in_1(in_3), .A(in_1[19]), .B(in_4[19]), .out_8(out_5[19]), .in_2(Subtract_Ctrl), .Cin(bit_alu_13_cout),
    .CMPEQ_IN(bit_alu_11_to_next_bit_alu), .Cout(bit_alu_12_cout),
    .To_next_Bit_ALU(bit_alu_12_to_next_bit_alu), .CMPLT___0(1'b0));
  Bit_ALU bit_alu_13 (
    .in_1(in_3), .A(in_1[18]), .B(in_4[18]), .out_8(out_5[18]), .in_2(Subtract_Ctrl), .Cin(bit_alu_14_cout),
    .CMPEQ_IN(bit_alu_12_to_next_bit_alu), .Cout(bit_alu_13_cout),
    .To_next_Bit_ALU(bit_alu_13_to_next_bit_alu), .CMPLT___0(1'b0));
  Bit_ALU bit_alu_14 (
    .in_1(in_3), .A(in_1[17]), .B(in_4[17]), .out_8(out_5[17]), .in_2(Subtract_Ctrl), .Cin(bit_alu_15_cout),
    .CMPEQ_IN(bit_alu_13_to_next_bit_alu), .Cout(bit_alu_14_cout),
    .To_next_Bit_ALU(bit_alu_14_to_next_bit_alu), .CMPLT___0(1'b0));
  Bit_ALU bit_alu_15 (
    .in_1(in_3), .A(in_1[16]), .B(in_4[16]), .out_8(out_5[16]), .in_2(Subtract_Ctrl), .Cin(bit_alu_16_cout),
    .CMPEQ_IN(bit_alu_14_to_next_bit_alu), .Cout(bit_alu_15_cout),
    .To_next_Bit_ALU(bit_alu_15_to_next_bit_alu), .CMPLT___0(1'b0));
  Bit_ALU bit_alu_16 (
    .in_1(in_3), .A(in_1[15]), .B(in_4[15]), .out_8(out_5[15]), .in_2(Subtract_Ctrl), .Cin(bit_alu_17_cout),
    .CMPEQ_IN(bit_alu_15_to_next_bit_alu), .Cout(bit_alu_16_cout),
    .To_next_Bit_ALU(bit_alu_16_to_next_bit_alu), .CMPLT___0(1'b0));
  Bit_ALU bit_alu_17 (
    .in_1(in_3), .A(in_1[14]), .B(in_4[14]), .out_8(out_5[14]), .in_2(Subtract_Ctrl), .Cin(bit_alu_18_cout),
    .CMPEQ_IN(bit_alu_16_to_next_bit_alu), .Cout(bit_alu_17_cout),
    .To_next_Bit_ALU(bit_alu_17_to_next_bit_alu), .CMPLT___0(1'b0));
  Bit_ALU bit_alu_18 (
    .in_1(in_3), .A(in_1[13]), .B(in_4[13]), .out_8(out_5[13]), .in_2(Subtract_Ctrl), .Cin(bit_alu_19_cout),
    .CMPEQ_IN(bit_alu_17_to_next_bit_alu), .Cout(bit_alu_18_cout),
    .To_next_Bit_ALU(bit_alu_18_to_next_bit_alu), .CMPLT___0(1'b0));
  Bit_ALU bit_alu_19 (
    .in_1(in_3), .A(in_1[12]), .B(in_4[12]), .out_8(out_5[12]), .in_2(Subtract_Ctrl), .Cin(bit_alu_20_cout),
    .CMPEQ_IN(bit_alu_18_to_next_bit_alu), .Cout(bit_alu_19_cout),
    .To_next_Bit_ALU(bit_alu_19_to_next_bit_alu), .CMPLT___0(1'b0));
  Bit_ALU bit_alu_20 (
    .in_1(in_3), .A(in_1[11]), .B(in_4[11]), .out_8(out_5[11]), .in_2(Subtract_Ctrl), .Cin(bit_alu_21_cout),
    .CMPEQ_IN(bit_alu_19_to_next_bit_alu), .Cout(bit_alu_20_cout),
    .To_next_Bit_ALU(bit_alu_20_to_next_bit_alu), .CMPLT___0(1'b0));
  Bit_ALU bit_alu_21 (
    .in_1(in_3), .A(in_1[10]), .B(in_4[10]), .out_8(out_5[10]), .in_2(Subtract_Ctrl), .Cin(bit_alu_22_cout),
    .CMPEQ_IN(bit_alu_20_to_next_bit_alu), .Cout(bit_alu_21_cout),
    .To_next_Bit_ALU(bit_alu_21_to_next_bit_alu), .CMPLT___0(1'b0));
  Bit_ALU bit_alu_22 (
    .in_1(in_3), .A(in_1[9]), .B(in_4[9]), .out_8(out_5[9]), .in_2(Subtract_Ctrl), .Cin(bit_alu_23_cout),
    .CMPEQ_IN(bit_alu_21_to_next_bit_alu), .Cout(bit_alu_22_cout),
    .To_next_Bit_ALU(bit_alu_22_to_next_bit_alu), .CMPLT___0(1'b0));
  Bit_ALU bit_alu_23 (
    .in_1(in_3), .A(in_1[8]), .B(in_4[8]), .out_8(out_5[8]), .in_2(Subtract_Ctrl), .Cin(bit_alu_24_cout),
    .CMPEQ_IN(bit_alu_22_to_next_bit_alu), .Cout(bit_alu_23_cout),
    .To_next_Bit_ALU(bit_alu_23_to_next_bit_alu), .CMPLT___0(1'b0));
  Bit_ALU bit_alu_24 (
    .in_1(in_3), .A(in_1[7]), .B(in_4[7]), .out_8(out_5[7]), .in_2(Subtract_Ctrl), .Cin(bit_alu_25_cout),
    .CMPEQ_IN(bit_alu_23_to_next_bit_alu), .Cout(bit_alu_24_cout),
    .To_next_Bit_ALU(bit_alu_24_to_next_bit_alu), .CMPLT___0(1'b0));
  Bit_ALU bit_alu_25 (
    .in_1(in_3), .A(in_1[6]), .B(in_4[6]), .out_8(out_5[6]), .in_2(Subtract_Ctrl), .Cin(bit_alu_26_cout),
    .CMPEQ_IN(bit_alu_24_to_next_bit_alu), .Cout(bit_alu_25_cout),
    .To_next_Bit_ALU(bit_alu_25_to_next_bit_alu), .CMPLT___0(1'b0));
  Bit_ALU bit_alu_26 (
    .in_1(in_3), .A(in_1[5]), .B(in_4[5]), .out_8(out_5[5]), .in_2(Subtract_Ctrl), .Cin(bit_alu_27_cout),
    .CMPEQ_IN(bit_alu_25_to_next_bit_alu), .Cout(bit_alu_26_cout),
    .To_next_Bit_ALU(bit_alu_26_to_next_bit_alu), .CMPLT___0(1'b0));
  Bit_ALU bit_alu_27 (
    .in_1(in_3), .A(in_1[4]), .B(in_4[4]), .out_8(out_5[4]), .in_2(Subtract_Ctrl), .Cin(bit_alu_28_cout),
    .CMPEQ_IN(bit_alu_26_to_next_bit_alu), .Cout(bit_alu_27_cout),
    .To_next_Bit_ALU(bit_alu_27_to_next_bit_alu), .CMPLT___0(1'b0));
  Bit_ALU bit_alu_28 (
    .in_1(in_3), .A(in_1[3]), .B(in_4[3]), .out_8(out_5[3]), .in_2(Subtract_Ctrl), .Cin(bit_alu_29_cout),
    .CMPEQ_IN(bit_alu_27_to_next_bit_alu), .Cout(bit_alu_28_cout),
    .To_next_Bit_ALU(bit_alu_28_to_next_bit_alu), .CMPLT___0(1'b0));
  Bit_ALU bit_alu_29 (
    .in_1(in_3), .A(in_1[2]), .B(in_4[2]), .out_8(out_5[2]), .in_2(Subtract_Ctrl), .Cin(bit_alu_30_cout),
    .CMPEQ_IN(bit_alu_28_to_next_bit_alu), .Cout(bit_alu_29_cout),
    .To_next_Bit_ALU(bit_alu_29_to_next_bit_alu), .CMPLT___0(1'b0));
  Bit_ALU bit_alu_30 (
    .in_1(in_3), .A(in_1[1]), .B(in_4[1]), .out_8(out_5[1]), .in_2(Subtract_Ctrl), .Cin(lsb_alu_1_cout),
    .CMPEQ_IN(bit_alu_29_to_next_bit_alu), .Cout(bit_alu_30_cout),
    .To_next_Bit_ALU(bit_alu_30_to_next_bit_alu), .CMPLT___0(1'b0));
  LSB_ALU lsb_alu_1 (
    .in_1(in_3), .in_6(in_1[0]), .in_7(in_4[0]), .out_8(out_5[0]), .in_2(Subtract_Ctrl),
    .CMPLT_IN(msb_alu_1_cmplt_out), .Cin(Subtract_Ctrl), .From_Bit_ALU_30(bit_alu_30_to_next_bit_alu),
    .out_9(lsb_alu_1_out_9), .Cout(lsb_alu_1_cout));
  MSB_ALU msb_alu_1 (
    .in_1(in_3), .A(in_1[31]), .B(in_4[31]), .out_7(out_5[31]), .in_2(Subtract_Ctrl),
    .CMPEQ_OUT(msb_alu_1_cmpeq_out), .CMPLT___0(1'b0), .Cin(bit_alu_1_cout), .CMPLT_OUT(msb_alu_1_cmplt_out));

  // Notes on the sheet:
  //   A
  //   B
  //   SUB => Bsel = 1
  //   CMPLE => Bsel = 1
  //   CMPLT => Bsel = 1
endmodule

module _32_X_32_Register_File (
  input  [4:0] in_1,
  input  Write_Enable,
  input  [31:0] in_3,
  input  CLK,
  input  [4:0] in_5,
  input  [4:0] Read_Address_B,
  output [31:0] out_7,
  output [31:0] out_8
);

  wire and_1_out, and_2_out, and_3_out, and_4_out, and_5_out, and_6_out, and_7_out, and_8_out, and_9_out,
       and_10_out, and_11_out, and_12_out, and_13_out, and_14_out, and_15_out, and_16_out, and_17_out,
       and_18_out, and_19_out, and_20_out, and_21_out, and_22_out, and_23_out, and_24_out, and_25_out,
       and_26_out, and_27_out, and_28_out, and_29_out, and_30_out, and_31_out, and_32_out, decoder_1_out0,
       decoder_1_out1, decoder_1_out2, decoder_1_out3, decoder_1_out4, decoder_1_out5, decoder_1_out6,
       decoder_1_out7, decoder_1_out8, decoder_1_out9, decoder_1_out10, decoder_1_out11, decoder_1_out12,
       decoder_1_out13, decoder_1_out14, decoder_1_out15, decoder_1_out16, decoder_1_out17, decoder_1_out18,
       decoder_1_out19, decoder_1_out20, decoder_1_out21, decoder_1_out22, decoder_1_out23, decoder_1_out24,
       decoder_1_out25, decoder_1_out26, decoder_1_out27, decoder_1_out28, decoder_1_out29, decoder_1_out30,
       decoder_1_out31;
  wire [31:0] buffer_1_out, buffer_2_out, buffer_3_out, buffer_4_out, buffer_5_out, buffer_6_out,
       buffer_7_out, buffer_8_out, buffer_9_out, buffer_10_out, buffer_11_out, buffer_12_out, buffer_13_out,
       buffer_14_out, buffer_15_out, buffer_16_out, buffer_17_out, buffer_18_out, buffer_19_out,
       buffer_20_out, buffer_21_out, buffer_22_out, buffer_23_out, buffer_24_out, buffer_25_out,
       buffer_26_out, buffer_27_out, buffer_28_out, buffer_29_out, buffer_30_out, buffer_31_out,
       buffer_32_out, n32_bit_register_1_out_4, n32_bit_register_2_out_4, n32_bit_register_3_out_4,
       n32_bit_register_4_out_4, n32_bit_register_5_out_4, n32_bit_register_6_out_4,
       n32_bit_register_7_out_4, n32_bit_register_8_out_4, n32_bit_register_9_out_4,
       n32_bit_register_10_out_4, n32_bit_register_11_out_4, n32_bit_register_12_out_4,
       n32_bit_register_13_out_4, n32_bit_register_14_out_4, n32_bit_register_15_out_4,
       n32_bit_register_16_out_4, n32_bit_register_17_out_4, n32_bit_register_18_out_4,
       n32_bit_register_19_out_4, n32_bit_register_20_out_4, n32_bit_register_21_out_4,
       n32_bit_register_22_out_4, n32_bit_register_23_out_4, n32_bit_register_24_out_4,
       n32_bit_register_25_out_4, n32_bit_register_26_out_4, n32_bit_register_27_out_4,
       n32_bit_register_28_out_4, n32_bit_register_29_out_4, n32_bit_register_30_out_4,
       n32_bit_register_31_out_4, n32_bit_register_32_out_4;

  and and_1 (and_1_out, decoder_1_out0, Write_Enable);
  _32_bit_register u_32_bit_register_1 (.in_1(in_3), .in_2(and_1_out), .out_4(n32_bit_register_1_out_4), .in_3(CLK));
  assign buffer_1_out = n32_bit_register_1_out_4;  // Buffer buffer_1, 32 bits wide
  and and_2 (and_2_out, decoder_1_out1, Write_Enable);
  _32_bit_register u_32_bit_register_2 (.in_1(in_3), .in_2(and_2_out), .out_4(n32_bit_register_2_out_4), .in_3(CLK));
  assign buffer_2_out = n32_bit_register_2_out_4;  // Buffer buffer_2, 32 bits wide
  Multiplexer #(.select(5), .width(32), .enable("false")) multiplexer_1 (
    .in0(buffer_1_out), .in1(buffer_2_out), .in2(buffer_3_out), .in3(buffer_4_out), .in4(buffer_5_out),
    .in5(buffer_6_out), .in6(buffer_7_out), .in7(buffer_8_out), .in8(buffer_9_out), .in9(buffer_10_out),
    .in10(buffer_11_out), .in11(buffer_12_out), .in12(buffer_13_out), .in13(buffer_14_out),
    .in14(buffer_15_out), .in15(buffer_16_out), .in16(buffer_17_out), .in17(buffer_18_out),
    .in18(buffer_19_out), .in19(buffer_20_out), .in20(buffer_21_out), .in21(buffer_22_out),
    .in22(buffer_23_out), .in23(buffer_24_out), .in24(buffer_25_out), .in25(buffer_26_out),
    .in26(buffer_27_out), .in27(buffer_28_out), .in28(buffer_29_out), .in29(buffer_30_out),
    .in30(buffer_31_out), .in31(buffer_32_out), .out(out_8), .sel(in_5));
  and and_3 (and_3_out, decoder_1_out2, Write_Enable);
  _32_bit_register u_32_bit_register_3 (.in_1(in_3), .in_2(and_3_out), .out_4(n32_bit_register_3_out_4), .in_3(CLK));
  assign buffer_3_out = n32_bit_register_3_out_4;  // Buffer buffer_3, 32 bits wide
  and and_4 (and_4_out, decoder_1_out3, Write_Enable);
  _32_bit_register u_32_bit_register_4 (.in_1(in_3), .in_2(and_4_out), .out_4(n32_bit_register_4_out_4), .in_3(CLK));
  assign buffer_4_out = n32_bit_register_4_out_4;  // Buffer buffer_4, 32 bits wide
  and and_5 (and_5_out, decoder_1_out4, Write_Enable);
  _32_bit_register u_32_bit_register_5 (.in_1(in_3), .in_2(and_5_out), .out_4(n32_bit_register_5_out_4), .in_3(CLK));
  assign buffer_5_out = n32_bit_register_5_out_4;  // Buffer buffer_5, 32 bits wide
  and and_6 (and_6_out, decoder_1_out5, Write_Enable);
  _32_bit_register u_32_bit_register_6 (.in_1(in_3), .in_2(and_6_out), .out_4(n32_bit_register_6_out_4), .in_3(CLK));
  assign buffer_6_out = n32_bit_register_6_out_4;  // Buffer buffer_6, 32 bits wide
  and and_7 (and_7_out, decoder_1_out6, Write_Enable);
  _32_bit_register u_32_bit_register_7 (.in_1(in_3), .in_2(and_7_out), .out_4(n32_bit_register_7_out_4), .in_3(CLK));
  assign buffer_7_out = n32_bit_register_7_out_4;  // Buffer buffer_7, 32 bits wide
  and and_8 (and_8_out, decoder_1_out7, Write_Enable);
  _32_bit_register u_32_bit_register_8 (.in_1(in_3), .in_2(and_8_out), .out_4(n32_bit_register_8_out_4), .in_3(CLK));
  assign buffer_8_out = n32_bit_register_8_out_4;  // Buffer buffer_8, 32 bits wide
  and and_9 (and_9_out, decoder_1_out8, Write_Enable);
  _32_bit_register u_32_bit_register_9 (.in_1(in_3), .in_2(and_9_out), .out_4(n32_bit_register_9_out_4), .in_3(CLK));
  assign buffer_9_out = n32_bit_register_9_out_4;  // Buffer buffer_9, 32 bits wide
  and and_10 (and_10_out, decoder_1_out9, Write_Enable);
  _32_bit_register u_32_bit_register_10 (.in_1(in_3), .in_2(and_10_out), .out_4(n32_bit_register_10_out_4), .in_3(CLK));
  assign buffer_10_out = n32_bit_register_10_out_4;  // Buffer buffer_10, 32 bits wide
  and and_11 (and_11_out, decoder_1_out10, Write_Enable);
  _32_bit_register u_32_bit_register_11 (.in_1(in_3), .in_2(and_11_out), .out_4(n32_bit_register_11_out_4), .in_3(CLK));
  assign buffer_11_out = n32_bit_register_11_out_4;  // Buffer buffer_11, 32 bits wide
  and and_12 (and_12_out, decoder_1_out11, Write_Enable);
  _32_bit_register u_32_bit_register_12 (.in_1(in_3), .in_2(and_12_out), .out_4(n32_bit_register_12_out_4), .in_3(CLK));
  assign buffer_12_out = n32_bit_register_12_out_4;  // Buffer buffer_12, 32 bits wide
  and and_13 (and_13_out, decoder_1_out12, Write_Enable);
  _32_bit_register u_32_bit_register_13 (.in_1(in_3), .in_2(and_13_out), .out_4(n32_bit_register_13_out_4), .in_3(CLK));
  assign buffer_13_out = n32_bit_register_13_out_4;  // Buffer buffer_13, 32 bits wide
  and and_14 (and_14_out, decoder_1_out13, Write_Enable);
  _32_bit_register u_32_bit_register_14 (.in_1(in_3), .in_2(and_14_out), .out_4(n32_bit_register_14_out_4), .in_3(CLK));
  assign buffer_14_out = n32_bit_register_14_out_4;  // Buffer buffer_14, 32 bits wide
  and and_15 (and_15_out, decoder_1_out14, Write_Enable);
  _32_bit_register u_32_bit_register_15 (.in_1(in_3), .in_2(and_15_out), .out_4(n32_bit_register_15_out_4), .in_3(CLK));
  assign buffer_15_out = n32_bit_register_15_out_4;  // Buffer buffer_15, 32 bits wide
  and and_16 (and_16_out, decoder_1_out15, Write_Enable);
  _32_bit_register u_32_bit_register_16 (.in_1(in_3), .in_2(and_16_out), .out_4(n32_bit_register_16_out_4), .in_3(CLK));
  assign buffer_16_out = n32_bit_register_16_out_4;  // Buffer buffer_16, 32 bits wide
  and and_17 (and_17_out, decoder_1_out16, Write_Enable);
  _32_bit_register u_32_bit_register_17 (.in_1(in_3), .in_2(and_17_out), .out_4(n32_bit_register_17_out_4), .in_3(CLK));
  assign buffer_17_out = n32_bit_register_17_out_4;  // Buffer buffer_17, 32 bits wide
  and and_18 (and_18_out, decoder_1_out17, Write_Enable);
  _32_bit_register u_32_bit_register_18 (.in_1(in_3), .in_2(and_18_out), .out_4(n32_bit_register_18_out_4), .in_3(CLK));
  assign buffer_18_out = n32_bit_register_18_out_4;  // Buffer buffer_18, 32 bits wide
  and and_19 (and_19_out, decoder_1_out18, Write_Enable);
  _32_bit_register u_32_bit_register_19 (.in_1(in_3), .in_2(and_19_out), .out_4(n32_bit_register_19_out_4), .in_3(CLK));
  assign buffer_19_out = n32_bit_register_19_out_4;  // Buffer buffer_19, 32 bits wide
  and and_20 (and_20_out, decoder_1_out19, Write_Enable);
  _32_bit_register u_32_bit_register_20 (.in_1(in_3), .in_2(and_20_out), .out_4(n32_bit_register_20_out_4), .in_3(CLK));
  assign buffer_20_out = n32_bit_register_20_out_4;  // Buffer buffer_20, 32 bits wide
  and and_21 (and_21_out, decoder_1_out20, Write_Enable);
  _32_bit_register u_32_bit_register_21 (.in_1(in_3), .in_2(and_21_out), .out_4(n32_bit_register_21_out_4), .in_3(CLK));
  assign buffer_21_out = n32_bit_register_21_out_4;  // Buffer buffer_21, 32 bits wide
  and and_22 (and_22_out, decoder_1_out21, Write_Enable);
  _32_bit_register u_32_bit_register_22 (.in_1(in_3), .in_2(and_22_out), .out_4(n32_bit_register_22_out_4), .in_3(CLK));
  assign buffer_22_out = n32_bit_register_22_out_4;  // Buffer buffer_22, 32 bits wide
  and and_23 (and_23_out, decoder_1_out22, Write_Enable);
  _32_bit_register u_32_bit_register_23 (.in_1(in_3), .in_2(and_23_out), .out_4(n32_bit_register_23_out_4), .in_3(CLK));
  assign buffer_23_out = n32_bit_register_23_out_4;  // Buffer buffer_23, 32 bits wide
  and and_24 (and_24_out, decoder_1_out23, Write_Enable);
  _32_bit_register u_32_bit_register_24 (.in_1(in_3), .in_2(and_24_out), .out_4(n32_bit_register_24_out_4), .in_3(CLK));
  assign buffer_24_out = n32_bit_register_24_out_4;  // Buffer buffer_24, 32 bits wide
  and and_25 (and_25_out, decoder_1_out24, Write_Enable);
  _32_bit_register u_32_bit_register_25 (.in_1(in_3), .in_2(and_25_out), .out_4(n32_bit_register_25_out_4), .in_3(CLK));
  assign buffer_25_out = n32_bit_register_25_out_4;  // Buffer buffer_25, 32 bits wide
  and and_26 (and_26_out, decoder_1_out25, Write_Enable);
  _32_bit_register u_32_bit_register_26 (.in_1(in_3), .in_2(and_26_out), .out_4(n32_bit_register_26_out_4), .in_3(CLK));
  assign buffer_26_out = n32_bit_register_26_out_4;  // Buffer buffer_26, 32 bits wide
  and and_27 (and_27_out, decoder_1_out26, Write_Enable);
  _32_bit_register u_32_bit_register_27 (.in_1(in_3), .in_2(and_27_out), .out_4(n32_bit_register_27_out_4), .in_3(CLK));
  assign buffer_27_out = n32_bit_register_27_out_4;  // Buffer buffer_27, 32 bits wide
  and and_28 (and_28_out, decoder_1_out27, Write_Enable);
  _32_bit_register u_32_bit_register_28 (.in_1(in_3), .in_2(and_28_out), .out_4(n32_bit_register_28_out_4), .in_3(CLK));
  assign buffer_28_out = n32_bit_register_28_out_4;  // Buffer buffer_28, 32 bits wide
  and and_29 (and_29_out, decoder_1_out28, Write_Enable);
  _32_bit_register u_32_bit_register_29 (.in_1(in_3), .in_2(and_29_out), .out_4(n32_bit_register_29_out_4), .in_3(CLK));
  assign buffer_29_out = n32_bit_register_29_out_4;  // Buffer buffer_29, 32 bits wide
  and and_30 (and_30_out, decoder_1_out29, Write_Enable);
  _32_bit_register u_32_bit_register_30 (.in_1(in_3), .in_2(and_30_out), .out_4(n32_bit_register_30_out_4), .in_3(CLK));
  assign buffer_30_out = n32_bit_register_30_out_4;  // Buffer buffer_30, 32 bits wide
  and and_31 (and_31_out, decoder_1_out30, Write_Enable);
  _32_bit_register u_32_bit_register_31 (.in_1(in_3), .in_2(and_31_out), .out_4(n32_bit_register_31_out_4), .in_3(CLK));
  assign buffer_31_out = n32_bit_register_31_out_4;  // Buffer buffer_31, 32 bits wide
  and and_32 (and_32_out, decoder_1_out31, Write_Enable);
  _32_bit_register u_32_bit_register_32 (
    .in_1({32{1'b0}}), .in_2(and_32_out), .out_4(n32_bit_register_32_out_4), .in_3(CLK));
  assign buffer_32_out = n32_bit_register_32_out_4;  // Buffer buffer_32, 32 bits wide
  Multiplexer #(.select(5), .width(32), .enable("false")) multiplexer_2 (
    .in0(buffer_1_out), .in1(buffer_2_out), .in2(buffer_3_out), .in3(buffer_4_out), .in4(buffer_5_out),
    .in5(buffer_6_out), .in6(buffer_7_out), .in7(buffer_8_out), .in8(buffer_9_out), .in9(buffer_10_out),
    .in10(buffer_11_out), .in11(buffer_12_out), .in12(buffer_13_out), .in13(buffer_14_out),
    .in14(buffer_15_out), .in15(buffer_16_out), .in16(buffer_17_out), .in17(buffer_18_out),
    .in18(buffer_19_out), .in19(buffer_20_out), .in20(buffer_21_out), .in21(buffer_22_out),
    .in22(buffer_23_out), .in23(buffer_24_out), .in24(buffer_25_out), .in25(buffer_26_out),
    .in26(buffer_27_out), .in27(buffer_28_out), .in28(buffer_29_out), .in29(buffer_30_out),
    .in30(buffer_31_out), .in31(buffer_32_out), .out(out_7), .sel(Read_Address_B));
  Decoder #(.select(5), .enable("false")) decoder_1 (
    .out0(decoder_1_out0), .out1(decoder_1_out1), .out2(decoder_1_out2), .out3(decoder_1_out3),
    .out4(decoder_1_out4), .out5(decoder_1_out5), .out6(decoder_1_out6), .out7(decoder_1_out7),
    .out8(decoder_1_out8), .out9(decoder_1_out9), .out10(decoder_1_out10), .out11(decoder_1_out11),
    .out12(decoder_1_out12), .out13(decoder_1_out13), .out14(decoder_1_out14), .out15(decoder_1_out15),
    .out16(decoder_1_out16), .out17(decoder_1_out17), .out18(decoder_1_out18), .out19(decoder_1_out19),
    .out20(decoder_1_out20), .out21(decoder_1_out21), .out22(decoder_1_out22), .out23(decoder_1_out23),
    .out24(decoder_1_out24), .out25(decoder_1_out25), .out26(decoder_1_out26), .out27(decoder_1_out27),
    .out28(decoder_1_out28), .out29(decoder_1_out29), .out30(decoder_1_out30), .out31(decoder_1_out31),
    .sel(in_1));

  // Notes on the sheet:
  //   Write Data
  //   Read Address A
  //   R0
  //   A
  //   R31
  //   B
  //   Write Address
endmodule

module Multiplier_Divider_Unit (
  input  [31:0] in_1,
  input  [31:0] in_2,
  input  in_3,
  output [31:0] out_4,
  output [31:0] out_5
);

  wire buffer_2_out, not_1_out;
  wire [31:0] buffer_1_out, controlled_buffer_1_out, controlled_buffer_2_out, controlled_buffer_3_out,
       controlled_buffer_4_out, divider_1_out, multiplier_1_out, not_2_out;

  not not_1 (not_1_out, buffer_2_out);
  assign controlled_buffer_1_out = not_1_out ? in_1 : 32'bz;  // Controlled_Buffer controlled_buffer_1
  assign controlled_buffer_2_out = not_1_out ? in_2 : 32'bz;  // Controlled_Buffer controlled_buffer_2
  assign controlled_buffer_3_out = buffer_2_out ? in_1 : 32'bz;  // Controlled_Buffer controlled_buffer_3
  assign controlled_buffer_4_out = buffer_2_out ? in_2 : 32'bz;  // Controlled_Buffer controlled_buffer_4
  assign buffer_1_out = {32{1'b0}};  // Buffer buffer_1, 32 bits wide
  Multiplier #(.width(32)) multiplier_1 (
    .a(controlled_buffer_1_out), .b(controlled_buffer_2_out), .out(multiplier_1_out), .cin(buffer_1_out),
    .cout(out_5));
  assign not_2_out = ~buffer_1_out;  // NOT_Gate not_2, 32 bits wide
  Multiplexer #(.width(32), .enable("false")) multiplexer_1 (
    .in0(multiplier_1_out), .in1(divider_1_out), .out(out_4), .sel(buffer_2_out));
  Divider #(.width(32)) divider_1 (
    .a(controlled_buffer_3_out), .b(controlled_buffer_4_out), .out(divider_1_out), .upper(not_2_out),
    .rem(out_5));
  buf buffer_2 (buffer_2_out, in_3);

  // Notes on the sheet:
  //   Input
  //   Input B
  //   Tristate Buffers for preventing unnecessary computation
  //   Multiplier and Divider Unit
  //   OUTPUT
endmodule

module Shift_Unit (
  input  [31:0] in_1,
  input  [4:0] in_2,
  input  [1:0] in_3,
  output [31:0] out_4
);

  wire [31:0] shifter_1_out, shifter_2_out, shifter_3_out;

  Shifter #(.width(32)) shifter_1 (.in(in_1), .\dist (in_2), .out(shifter_1_out));
  Shifter #(.width(32), .shift("lr")) shifter_2 (.in(in_1), .\dist (in_2), .out(shifter_2_out));
  Shifter #(.width(32), .shift("ar")) shifter_3 (.in(in_1), .\dist (in_2), .out(shifter_3_out));
  Multiplexer #(.select(2), .width(32), .enable("false")) multiplexer_1 (
    .in0(shifter_1_out), .in1(shifter_2_out), .in2(shifter_3_out), .out(out_4), .sel(in_3));  // open: in3
endmodule

module Final_Datapath (
);

  wire Clock, control_pla_1_aluopa, control_pla_1_instrregen, control_pla_1_mult_divctrl,
       control_pla_1_out_4, control_pla_1_out_5, control_pla_1_out_17, control_pla_1_out_18,
       control_pla_1_pcen, control_pla_1_pcsrc, control_pla_1_shiftopa, control_pla_1_subtractctrl;
  wire [1:0] control_pla_1_shiftctrl, control_pla_1_shiftopb;
  wire [2:0] control_pla_1_aluctrl, control_pla_1_out_13, control_pla_1_out_19;
  wire [4:0] multiplexer_1_out, multiplexer_6_out;
  wire [5:0] control_pla_1_ns0, register_3_q;
  wire [31:0] bit_extender_1_out, final_alu32_1_out_5, multiplexer_2_out, multiplexer_3_out,
       multiplexer_4_out, multiplexer_5_out, multiplexer_7_out, multiplier_divider_unit_1_out_4,
       n32_x_32_register_file_1_out_7, n32_x_32_register_file_1_out_8, not_1_out, ram_1_data, register_1_q,
       register_2_q, register_4_q, register_5_q, register_6_q, register_7_q, register_8_q, register_9_q,
       rom_1_data, shift_unit_1_out_4;

  Register #(.width(32)) register_1 (
    .D(multiplexer_7_out), .en(control_pla_1_pcen), .Q(register_1_q), .clk(Clock));  // open: clr
  Clock clock_1 (.out(Clock));
  ROM #(.addrWidth(24), .dataWidth(32)) rom_1 (.addr(register_1_q[23:0]), .data(rom_1_data), .sel(1'b1));
  Register #(.width(32)) register_2 (
    .D(rom_1_data), .en(control_pla_1_instrregen), .Q(register_2_q), .clk(Clock));  // open: clr
  Multiplexer #(.width(5), .enable("false")) multiplexer_1 (
    .in0(register_2_q[15:11]), .in1(register_2_q[25:21]), .out(multiplexer_1_out), .sel(control_pla_1_out_17));
  Multiplexer #(.select(3), .width(32), .enable("false")) multiplexer_2 (
    .in0(register_9_q), .in1(register_8_q), .in2(register_7_q), .in3(register_6_q), .in4(multiplexer_7_out),
    .in5(register_1_q), .out(multiplexer_2_out), .sel(control_pla_1_out_19));  // open: in6, in7
  Control_PLA control_pla_1 (
    .States(register_3_q), .Opcodes(register_2_q[31:26]), .out_4(control_pla_1_out_4),
    .out_5(control_pla_1_out_5), .PCSrc(control_pla_1_pcsrc), .MULT_DIVCtrl(control_pla_1_mult_divctrl),
    .SHIFTCtrl(control_pla_1_shiftctrl), .SHIFTOpB(control_pla_1_shiftopb),
    .SHIFTOpA(control_pla_1_shiftopa), .SubtractCtrl(control_pla_1_subtractctrl),
    .ALUCtrl(control_pla_1_aluctrl), .out_13(control_pla_1_out_13), .ALUOpA(control_pla_1_aluopa),
    .PCEN(control_pla_1_pcen), .InstrRegEN(control_pla_1_instrregen), .out_17(control_pla_1_out_17),
    .out_18(control_pla_1_out_18), .out_19(control_pla_1_out_19), .in_2(not_1_out),
    .NS0(control_pla_1_ns0[0]), .NS1(control_pla_1_ns0[1]), .NS2(control_pla_1_ns0[2]),
    .NS3(control_pla_1_ns0[3]), .NS4(control_pla_1_ns0[4]), .NS5(control_pla_1_ns0[5]));
  Register #(.width(6)) register_3 (.D(control_pla_1_ns0), .Q(register_3_q), .clk(Clock));  // open: en, clr
  _32_X_32_Register_File u_32_x_32_register_file_1 (
    .in_3(multiplexer_2_out), .in_1(register_2_q[25:21]), .Write_Enable(control_pla_1_out_18),
    .in_5(register_2_q[20:16]), .out_8(n32_x_32_register_file_1_out_8), .Read_Address_B(multiplexer_1_out),
    .out_7(n32_x_32_register_file_1_out_7), .CLK(Clock));
  assign bit_extender_1_out = {{16{register_2_q[15]}}, register_2_q[15:0]};  // Bit_Extender bit_extender_1
  assign not_1_out = ~register_4_q;  // NOT_Gate not_1, 32 bits wide
  Register #(.width(32)) register_4 (
    .D(n32_x_32_register_file_1_out_8), .Q(register_4_q), .clr(Clock));  // open: en, clk
  Register #(.width(32)) register_5 (
    .D(n32_x_32_register_file_1_out_7), .Q(register_5_q), .clk(Clock));  // open: en, clr
  Multiplexer #(.select(3), .width(32), .enable("false")) multiplexer_3 (
    .in0(register_5_q), .in1(bit_extender_1_out), .in2(shift_unit_1_out_4), .in3(32'h4), .in4(32'hfffffffc),
    .out(multiplexer_3_out), .sel(control_pla_1_out_13));  // open: in5, in6, in7
  Multiplexer #(.width(32), .enable("false")) multiplexer_4 (
    .in0(register_4_q), .in1(bit_extender_1_out), .out(multiplexer_4_out), .sel(control_pla_1_shiftopa));
  Multiplexer #(.width(32), .enable("false")) multiplexer_5 (
    .in0(register_4_q), .in1(register_1_q), .out(multiplexer_5_out), .sel(control_pla_1_aluopa));
  Multiplier_Divider_Unit multiplier_divider_unit_1 (
    .in_1(register_4_q), .in_2(multiplexer_3_out), .out_4(multiplier_divider_unit_1_out_4),
    .in_3(control_pla_1_mult_divctrl));  // open: out_5
  Multiplexer #(.select(2), .width(5), .enable("false")) multiplexer_6 (
    .in0(multiplexer_3_out[4:0]), .in1(register_2_q[4:0]), .in2(5'b00010), .out(multiplexer_6_out),
    .sel(control_pla_1_shiftopb));  // open: in3
  Register #(.width(32)) register_6 (
    .D(multiplier_divider_unit_1_out_4), .Q(register_6_q), .clk(Clock));  // open: en, clr
  Shift_Unit shift_unit_1 (
    .in_1(multiplexer_4_out), .out_4(shift_unit_1_out_4), .in_2(multiplexer_6_out),
    .in_3(control_pla_1_shiftctrl));
  Register #(.width(32)) register_7 (.D(shift_unit_1_out_4), .Q(register_7_q), .clk(Clock));  // open: en, clr
  Final_ALU32 final_alu32_1 (
    .in_1(multiplexer_5_out), .in_4(multiplexer_3_out), .out_5(final_alu32_1_out_5),
    .Subtract_Ctrl(control_pla_1_subtractctrl), .in_3(control_pla_1_aluctrl));
  Register #(.width(32)) register_8 (.D(final_alu32_1_out_5), .Q(register_8_q), .clk(Clock));  // open: en, clr
  Multiplexer #(.width(32), .enable("false")) multiplexer_7 (
    .in0(final_alu32_1_out_5), .in1(register_8_q), .out(multiplexer_7_out), .sel(control_pla_1_pcsrc));
  RAM #(.addrWidth(24), .dataWidth(32), .bus("separate")) ram_1 (
    .addr(register_8_q[23:0]), .din(register_5_q), .data(ram_1_data), .str(control_pla_1_out_5), .clk(Clock),
    .ld(control_pla_1_out_4));  // open: sel, clr
  Register #(.width(32)) register_9 (.D(ram_1_data), .Q(register_9_q), .clk(Clock));  // open: en, clr

  // Notes on the sheet:
  //   PC
  //   contents of rom_1 (hex, n*v repeats v):
  //   7000fff7 0 0 0 80000800
  //   With Literal
  //   Store = 1
  //   From ALU for Rc
  //   Sign Extend
  //   Jump Instr EA
  //   PC Increment
  //   Multiply by 4 SHL
endmodule

module _32_bit_register (
  input  [31:0] in_1,
  input  in_2,
  input  in_3,
  output [31:0] out_4
);

  Register #(.width(32)) register_1 (.D(in_1), .en(in_2), .Q(out_4), .clk(in_3));  // open: clr
endmodule

module Control_PLA (
  input  [5:0] States,
  input  [31:0] in_2,
  input  [5:0] Opcodes,
  output out_4,
  output out_5,
  output PCSrc,
  output MULT_DIVCtrl,
  output [1:0] SHIFTCtrl,
  output [1:0] SHIFTOpB,
  output SHIFTOpA,
  output SubtractCtrl,
  output [2:0] ALUCtrl,
  output [2:0] out_13,
  output ALUOpA,
  output PCEN,
  output InstrRegEN,
  output out_17,
  output out_18,
  output [2:0] out_19,
  output NS0,
  output NS1,
  output NS2,
  output NS3,
  output NS4,
  output NS5
);

  wire ADD_out, ADDC_out, and_2_out, and_3_out, and_4_out, and_5_out, and_6_out, and_7_out, and_8_out,
       and_9_out, and_10_out, and_11_out, and_12_out, and_13_out, and_14_out, and_15_out, and_16_out,
       and_17_out, and_18_out, and_19_out, and_20_out, and_21_out, and_22_out, and_23_out, and_24_out,
       and_25_out, and_26_out, and_27_out, and_28_out, and_29_out, and_30_out, and_31_out, and_32_out,
       and_33_out, and_34_out, and_35_out, and_36_out, and_37_out, and_38_out, and_39_out, AND_out, ANDC_out,
       BEQ_BF_out, BNE_BT_out, CMPEQ_out, CMPEQC_out, CMPLE_out, CMPLEC_out, CMPLT_out, CMPLTC_out, DIV_out,
       DIVC_out, JMP_out, LD_out, LDR_out, MUL_out, MULC_out, or_2_out, or_3_out, or_4_out, or_5_out,
       or_6_out, or_7_out, or_8_out, or_9_out, or_10_out, OR_out, ORC_out, SHL_out, SHLC_out, SHR_out,
       SHRC_out, SRA_out, SRAC_out, ST_out, State2_out, State3_out, State4_out, State5_out, State6_out,
       State7_out, State8_out, State9_out, State10_out, State11_out, State12_out, State13_out, State14_out,
       State15_out, State16_out, State17_out, State18_out, State19_out, State20_out, State21_out,
       State22_out, State23_out, State24_out, State25_out, State26_out, State27_out, State28_out,
       State29_out, State30_out, State31_out, State34_out, State35_out, State37_out, State38_out, SUB_out,
       SUBC_out, XNOR_out, XNORC_out, XOR_out, XORC_out;
  wire [5:0] buffer_1_out, buffer_2_out;

  assign buffer_1_out = Opcodes;  // Buffer buffer_1, 6 bits wide
  and XNORC (XNORC_out, buffer_1_out[0], buffer_1_out[1], ~buffer_1_out[2], buffer_1_out[3], buffer_1_out[4], buffer_1_out[5]);  // AND_Gate
  and XNOR (XNOR_out, buffer_1_out[0], buffer_1_out[1], ~buffer_1_out[2], buffer_1_out[3], ~buffer_1_out[4], buffer_1_out[5]);  // AND_Gate
  and XORC (XORC_out, ~buffer_1_out[0], buffer_1_out[1], ~buffer_1_out[2], buffer_1_out[3], buffer_1_out[4], buffer_1_out[5]);  // AND_Gate
  and XOR (XOR_out, ~buffer_1_out[0], buffer_1_out[1], ~buffer_1_out[2], buffer_1_out[3], ~buffer_1_out[4], buffer_1_out[5]);  // AND_Gate
  and SUBC (SUBC_out, buffer_1_out[0], ~buffer_1_out[1], ~buffer_1_out[2], ~buffer_1_out[3], buffer_1_out[4], buffer_1_out[5]);  // AND_Gate
  and SUB (SUB_out, buffer_1_out[0], ~buffer_1_out[1], ~buffer_1_out[2], ~buffer_1_out[3], ~buffer_1_out[4], buffer_1_out[5]);  // AND_Gate
  and ST (ST_out, buffer_1_out[0], ~buffer_1_out[1], ~buffer_1_out[2], buffer_1_out[3], buffer_1_out[4], ~buffer_1_out[5]);  // AND_Gate
  and SRAC (SRAC_out, ~buffer_1_out[0], buffer_1_out[1], buffer_1_out[2], buffer_1_out[3], buffer_1_out[4], buffer_1_out[5]);  // AND_Gate
  and SRA (SRA_out, ~buffer_1_out[0], buffer_1_out[1], buffer_1_out[2], buffer_1_out[3], ~buffer_1_out[4], buffer_1_out[5]);  // AND_Gate
  and SHRC (SHRC_out, buffer_1_out[0], ~buffer_1_out[1], buffer_1_out[2], buffer_1_out[3], buffer_1_out[4], buffer_1_out[5]);  // AND_Gate
  and SHR (SHR_out, buffer_1_out[0], ~buffer_1_out[1], buffer_1_out[2], buffer_1_out[3], ~buffer_1_out[4], buffer_1_out[5]);  // AND_Gate
  and SHLC (SHLC_out, ~buffer_1_out[0], ~buffer_1_out[1], buffer_1_out[2], buffer_1_out[3], buffer_1_out[4], buffer_1_out[5]);  // AND_Gate
  and SHL (SHL_out, ~buffer_1_out[0], ~buffer_1_out[1], buffer_1_out[2], buffer_1_out[3], ~buffer_1_out[4], buffer_1_out[5]);  // AND_Gate
  and ORC (ORC_out, buffer_1_out[0], ~buffer_1_out[1], ~buffer_1_out[2], buffer_1_out[3], buffer_1_out[4], buffer_1_out[5]);  // AND_Gate
  and OR (OR_out, buffer_1_out[0], ~buffer_1_out[1], ~buffer_1_out[2], buffer_1_out[3], ~buffer_1_out[4], buffer_1_out[5]);  // AND_Gate
  and MULC (MULC_out, ~buffer_1_out[0], buffer_1_out[1], ~buffer_1_out[2], ~buffer_1_out[3], buffer_1_out[4], buffer_1_out[5]);  // AND_Gate
  and MUL (MUL_out, ~buffer_1_out[0], buffer_1_out[1], ~buffer_1_out[2], ~buffer_1_out[3], ~buffer_1_out[4], buffer_1_out[5]);  // AND_Gate
  and LDR (LDR_out, buffer_1_out[0], buffer_1_out[1], buffer_1_out[2], buffer_1_out[3], buffer_1_out[4], ~buffer_1_out[5]);  // AND_Gate
  and LD (LD_out, ~buffer_1_out[0], ~buffer_1_out[1], ~buffer_1_out[2], buffer_1_out[3], buffer_1_out[4], ~buffer_1_out[5]);  // AND_Gate
  and JMP (JMP_out, buffer_1_out[0], buffer_1_out[1], ~buffer_1_out[2], buffer_1_out[3], buffer_1_out[4], ~buffer_1_out[5]);  // AND_Gate
  and DIVC (DIVC_out, buffer_1_out[0], buffer_1_out[1], ~buffer_1_out[2], ~buffer_1_out[3], buffer_1_out[4], buffer_1_out[5]);  // AND_Gate
  and DIV (DIV_out, buffer_1_out[0], buffer_1_out[1], ~buffer_1_out[2], ~buffer_1_out[3], ~buffer_1_out[4], buffer_1_out[5]);  // AND_Gate
  and CMPLTC (CMPLTC_out, buffer_1_out[0], ~buffer_1_out[1], buffer_1_out[2], ~buffer_1_out[3], buffer_1_out[4], buffer_1_out[5]);  // AND_Gate
  and CMPLT (CMPLT_out, buffer_1_out[0], ~buffer_1_out[1], buffer_1_out[2], ~buffer_1_out[3], ~buffer_1_out[4], buffer_1_out[5]);  // AND_Gate
  and CMPLEC (CMPLEC_out, ~buffer_1_out[0], buffer_1_out[1], buffer_1_out[2], ~buffer_1_out[3], buffer_1_out[4], buffer_1_out[5]);  // AND_Gate
  and CMPLE (CMPLE_out, ~buffer_1_out[0], buffer_1_out[1], buffer_1_out[2], ~buffer_1_out[3], ~buffer_1_out[4], buffer_1_out[5]);  // AND_Gate
  and CMPEQC (CMPEQC_out, ~buffer_1_out[0], ~buffer_1_out[1], buffer_1_out[2], ~buffer_1_out[3], buffer_1_out[4], buffer_1_out[5]);  // AND_Gate
  and CMPEQ (CMPEQ_out, ~buffer_1_out[0], ~buffer_1_out[1], buffer_1_out[2], ~buffer_1_out[3], ~buffer_1_out[4], buffer_1_out[5]);  // AND_Gate
  and BNE_BT (BNE_BT_out, buffer_1_out[0], ~buffer_1_out[1], buffer_1_out[2], buffer_1_out[3], buffer_1_out[4], ~buffer_1_out[5]);  // AND_Gate
  and BEQ_BF (BEQ_BF_out, ~buffer_1_out[0], ~buffer_1_out[1], buffer_1_out[2], buffer_1_out[3], buffer_1_out[4], ~buffer_1_out[5]);  // AND_Gate
  and ANDC (ANDC_out, ~buffer_1_out[0], ~buffer_1_out[1], ~buffer_1_out[2], buffer_1_out[3], buffer_1_out[4], buffer_1_out[5]);  // AND_Gate
  and AND (AND_out, ~buffer_1_out[0], ~buffer_1_out[1], ~buffer_1_out[2], buffer_1_out[3], ~buffer_1_out[4], buffer_1_out[5]);  // AND_Gate
  and ADDC (ADDC_out, ~buffer_1_out[0], ~buffer_1_out[1], ~buffer_1_out[2], ~buffer_1_out[3], buffer_1_out[4], buffer_1_out[5]);  // AND_Gate
  and ADD (ADD_out, ~buffer_1_out[0], ~buffer_1_out[1], ~buffer_1_out[2], ~buffer_1_out[3], ~buffer_1_out[4], buffer_1_out[5]);  // AND_Gate
  assign buffer_2_out = States;  // Buffer buffer_2, 6 bits wide
  and State0 (InstrRegEN, ~buffer_2_out[5], ~buffer_2_out[4], ~buffer_2_out[3], ~buffer_2_out[2], ~buffer_2_out[1], ~buffer_2_out[0]);  // AND_Gate
  and State1 (SHIFTOpB[1], ~buffer_2_out[5], ~buffer_2_out[4], ~buffer_2_out[3], ~buffer_2_out[2], ~buffer_2_out[1], buffer_2_out[0]);  // AND_Gate
  and State2 (State2_out, ~buffer_2_out[5], ~buffer_2_out[4], ~buffer_2_out[3], ~buffer_2_out[2], buffer_2_out[1], ~buffer_2_out[0]);  // AND_Gate
  and State3 (State3_out, ~buffer_2_out[5], ~buffer_2_out[4], ~buffer_2_out[3], ~buffer_2_out[2], buffer_2_out[1], buffer_2_out[0]);  // AND_Gate
  and State4 (State4_out, ~buffer_2_out[5], ~buffer_2_out[4], ~buffer_2_out[3], buffer_2_out[2], ~buffer_2_out[1], ~buffer_2_out[0]);  // AND_Gate
  and State5 (State5_out, ~buffer_2_out[5], ~buffer_2_out[4], ~buffer_2_out[3], buffer_2_out[2], ~buffer_2_out[1], buffer_2_out[0]);  // AND_Gate
  and State6 (State6_out, ~buffer_2_out[5], ~buffer_2_out[4], ~buffer_2_out[3], buffer_2_out[2], buffer_2_out[1], ~buffer_2_out[0]);  // AND_Gate
  and State7 (State7_out, ~buffer_2_out[5], ~buffer_2_out[4], ~buffer_2_out[3], buffer_2_out[2], buffer_2_out[1], buffer_2_out[0]);  // AND_Gate
  and State8 (State8_out, ~buffer_2_out[5], ~buffer_2_out[4], buffer_2_out[3], ~buffer_2_out[2], ~buffer_2_out[1], ~buffer_2_out[0]);  // AND_Gate
  and State9 (State9_out, ~buffer_2_out[5], ~buffer_2_out[4], buffer_2_out[3], ~buffer_2_out[2], ~buffer_2_out[1], buffer_2_out[0]);  // AND_Gate
  and State10 (State10_out, ~buffer_2_out[5], ~buffer_2_out[4], buffer_2_out[3], ~buffer_2_out[2], buffer_2_out[1], ~buffer_2_out[0]);  // AND_Gate
  and State11 (State11_out, ~buffer_2_out[5], ~buffer_2_out[4], buffer_2_out[3], ~buffer_2_out[2], buffer_2_out[1], buffer_2_out[0]);  // AND_Gate
  and State12 (State12_out, ~buffer_2_out[5], ~buffer_2_out[4], buffer_2_out[3], buffer_2_out[2], ~buffer_2_out[1], ~buffer_2_out[0]);  // AND_Gate
  and State13 (State13_out, ~buffer_2_out[5], ~buffer_2_out[4], buffer_2_out[3], buffer_2_out[2], ~buffer_2_out[1], buffer_2_out[0]);  // AND_Gate
  and State14 (State14_out, ~buffer_2_out[5], ~buffer_2_out[4], buffer_2_out[3], buffer_2_out[2], buffer_2_out[1], ~buffer_2_out[0]);  // AND_Gate
  and State15 (State15_out, ~buffer_2_out[5], ~buffer_2_out[4], buffer_2_out[3], buffer_2_out[2], buffer_2_out[1], buffer_2_out[0]);  // AND_Gate
  and State16 (State16_out, ~buffer_2_out[5], buffer_2_out[4], ~buffer_2_out[3], ~buffer_2_out[2], ~buffer_2_out[1], ~buffer_2_out[0]);  // AND_Gate
  and State17 (State17_out, ~buffer_2_out[5], buffer_2_out[4], ~buffer_2_out[3], ~buffer_2_out[2], ~buffer_2_out[1], buffer_2_out[0]);  // AND_Gate
  and State18 (State18_out, ~buffer_2_out[5], buffer_2_out[4], ~buffer_2_out[3], ~buffer_2_out[2], buffer_2_out[1], ~buffer_2_out[0]);  // AND_Gate
  and State19 (State19_out, ~buffer_2_out[5], buffer_2_out[4], ~buffer_2_out[3], ~buffer_2_out[2], buffer_2_out[1], buffer_2_out[0]);  // AND_Gate
  and State20 (State20_out, ~buffer_2_out[5], buffer_2_out[4], ~buffer_2_out[3], buffer_2_out[2], ~buffer_2_out[1], ~buffer_2_out[0]);  // AND_Gate
  and State21 (State21_out, ~buffer_2_out[5], buffer_2_out[4], ~buffer_2_out[3], buffer_2_out[2], ~buffer_2_out[1], buffer_2_out[0]);  // AND_Gate
  and State22 (State22_out, ~buffer_2_out[5], buffer_2_out[4], ~buffer_2_out[3], buffer_2_out[2], buffer_2_out[1], ~buffer_2_out[0]);  // AND_Gate
  and State23 (State23_out, ~buffer_2_out[5], buffer_2_out[4], ~buffer_2_out[3], buffer_2_out[2], buffer_2_out[1], buffer_2_out[0]);  // AND_Gate
  and State24 (State24_out, ~buffer_2_out[5], buffer_2_out[4], buffer_2_out[3], ~buffer_2_out[2], ~buffer_2_out[1], ~buffer_2_out[0]);  // AND_Gate
  and State25 (State25_out, ~buffer_2_out[5], buffer_2_out[4], buffer_2_out[3], ~buffer_2_out[2], ~buffer_2_out[1], buffer_2_out[0]);  // AND_Gate
  and State26 (State26_out, ~buffer_2_out[5], buffer_2_out[4], buffer_2_out[3], ~buffer_2_out[2], buffer_2_out[1], ~buffer_2_out[0]);  // AND_Gate
  or or_2 (or_2_out, MULC_out, MUL_out, DIVC_out, DIV_out);
  and State27 (State27_out, ~buffer_2_out[5], buffer_2_out[4], buffer_2_out[3], ~buffer_2_out[2], buffer_2_out[1], buffer_2_out[0]);  // AND_Gate
  and State28 (State28_out, ~buffer_2_out[5], buffer_2_out[4], buffer_2_out[3], buffer_2_out[2], ~buffer_2_out[1], ~buffer_2_out[0]);  // AND_Gate
  and State29 (State29_out, ~buffer_2_out[5], buffer_2_out[4], buffer_2_out[3], buffer_2_out[2], ~buffer_2_out[1], buffer_2_out[0]);  // AND_Gate
  and State30 (State30_out, ~buffer_2_out[5], buffer_2_out[4], buffer_2_out[3], buffer_2_out[2], buffer_2_out[1], ~buffer_2_out[0]);  // AND_Gate
  and State31 (State31_out, ~buffer_2_out[5], buffer_2_out[4], buffer_2_out[3], buffer_2_out[2], buffer_2_out[1], buffer_2_out[0]);  // AND_Gate
  or or_3 (or_3_out, State24_out, State23_out, State22_out, State21_out, State20_out, State19_out);
  or or_4 (or_4_out, SRAC_out, SRA_out, SHRC_out, SHR_out, SHLC_out, SHL_out);
  or or_5 (or_5_out, ST_out, LD_out);
  and State32 (out_5, buffer_2_out[5], ~buffer_2_out[4], ~buffer_2_out[3], ~buffer_2_out[2], ~buffer_2_out[1], ~buffer_2_out[0]);  // AND_Gate
  and State33 (out_4, buffer_2_out[5], ~buffer_2_out[4], ~buffer_2_out[3], ~buffer_2_out[2], ~buffer_2_out[1], buffer_2_out[0]);  // AND_Gate
  or or_6 (or_6_out, State16_out, State15_out, State14_out, State13_out);
  and State34 (State34_out, buffer_2_out[5], ~buffer_2_out[4], ~buffer_2_out[3], ~buffer_2_out[2], buffer_2_out[1], ~buffer_2_out[0]);  // AND_Gate
  or or_7 (or_7_out, State30_out, State29_out, State28_out, State27_out, State26_out, State25_out, State18_out, State17_out, State12_out, State11_out, State10_out, State9_out, State8_out, State7_out, State6_out, State5_out, State4_out, State2_out);
  or or_8 (or_8_out, XNORC_out, XNOR_out, XORC_out, XOR_out, SUBC_out, SUB_out, ORC_out, OR_out, CMPLTC_out, CMPLT_out, CMPLEC_out, CMPLE_out, CMPEQC_out, CMPEQ_out, ANDC_out, AND_out, ADDC_out, ADD_out);
  and State35 (State35_out, buffer_2_out[5], ~buffer_2_out[4], ~buffer_2_out[3], ~buffer_2_out[2], buffer_2_out[1], buffer_2_out[0]);  // AND_Gate
  and and_2 (and_2_out, or_6_out, or_2_out);
  and and_3 (and_3_out, SHIFTOpB[1], XNORC_out);
  and and_4 (and_4_out, SHIFTOpB[1], XNOR_out);
  and and_5 (and_5_out, SHIFTOpB[1], XORC_out);
  and and_6 (and_6_out, SHIFTOpB[1], XOR_out);
  and and_7 (and_7_out, SHIFTOpB[1], SUBC_out);
  and and_8 (and_8_out, SHIFTOpB[1], SUB_out);
  and and_9 (and_9_out, State31_out, ST_out);
  and and_10 (and_10_out, SHIFTOpB[1], SRAC_out);
  and and_11 (and_11_out, SHIFTOpB[1], SRA_out);
  and and_12 (and_12_out, SHIFTOpB[1], SHRC_out);
  and and_13 (and_13_out, SHIFTOpB[1], SHR_out);
  and and_14 (and_14_out, SHIFTOpB[1], SHLC_out);
  and and_15 (and_15_out, SHIFTOpB[1], SHL_out);
  and and_16 (and_16_out, SHIFTOpB[1], ORC_out);
  and and_17 (and_17_out, SHIFTOpB[1], OR_out);
  and and_18 (and_18_out, SHIFTOpB[1], MULC_out);
  and and_19 (and_19_out, SHIFTOpB[1], MUL_out);
  or or_9 (or_9_out, SHIFTOpB[1], State31_out);
  or or_10 (or_10_out, LDR_out, LD_out);
  and and_20 (and_20_out, SHIFTOpB[1], or_5_out);
  and and_21 (and_21_out, SHIFTOpB[1], JMP_out);
  and and_22 (and_22_out, SHIFTOpB[1], DIVC_out);
  and and_23 (and_23_out, SHIFTOpB[1], DIV_out);
  and and_24 (and_24_out, SHIFTOpB[1], CMPLTC_out);
  and and_25 (and_25_out, SHIFTOpB[1], CMPLT_out);
  and and_26 (and_26_out, SHIFTOpB[1], CMPLEC_out);
  and and_27 (and_27_out, SHIFTOpB[1], CMPLE_out);
  and and_28 (and_28_out, SHIFTOpB[1], CMPEQC_out);
  and and_29 (and_29_out, SHIFTOpB[1], CMPEQ_out);
  and and_30 (and_30_out, SHIFTOpB[1], and_39_out, BNE_BT_out);
  and and_31 (and_31_out, SHIFTOpB[1], and_39_out, BEQ_BF_out);
  and and_32 (and_32_out, SHIFTOpB[1], ANDC_out);
  and and_33 (and_33_out, SHIFTOpB[1], AND_out);
  and and_34 (and_34_out, SHIFTOpB[1], ADDC_out);
  and and_35 (and_35_out, SHIFTOpB[1], ADD_out);
  and State36 (out_13[2], buffer_2_out[5], ~buffer_2_out[4], ~buffer_2_out[3], buffer_2_out[2], ~buffer_2_out[1], ~buffer_2_out[0]);  // AND_Gate
  and and_36 (and_36_out, or_9_out, or_10_out);
  and State37 (State37_out, buffer_2_out[5], ~buffer_2_out[4], ~buffer_2_out[3], buffer_2_out[2], ~buffer_2_out[1], buffer_2_out[0]);  // AND_Gate
  and and_37 (and_37_out, or_7_out, or_8_out);
  and and_38 (and_38_out, or_3_out, or_4_out);
  and State38 (State38_out, buffer_2_out[5], ~buffer_2_out[4], ~buffer_2_out[3], buffer_2_out[2], buffer_2_out[1], ~buffer_2_out[0]);  // AND_Gate
  or or_11 (SHIFTOpB[0], State24_out, State22_out, State20_out);
  or or_12 (out_19[2], out_13[2], State35_out, State34_out);
  or or_13 (MULT_DIVCtrl, State14_out, State13_out);
  or or_14 (SHIFTCtrl[1], State24_out, State23_out);
  or or_15 (SHIFTCtrl[0], State22_out, State21_out);
  or or_16 (SHIFTOpA, SHIFTOpB[0], SHIFTOpB[1]);
  or or_17 (SubtractCtrl, State26_out, State25_out, State12_out, State11_out, State10_out, State9_out);
  or or_18 (ALUCtrl[2], State26_out, State25_out, State12_out, State11_out, State8_out, State31_out, SHIFTOpB[1], State7_out, State10_out, State9_out, State4_out, InstrRegEN, State2_out);
  or or_19 (ALUCtrl[1], State29_out, State27_out, State30_out, State28_out, State12_out, State11_out, State10_out, State9_out);
  or or_20 (ALUCtrl[0], State30_out, State29_out, State18_out, State17_out, State12_out, State11_out, State8_out, State7_out);
  or or_21 (ALUOpA, SHIFTOpB[1], InstrRegEN);
  or or_22 (out_13[0], State31_out, State30_out, State28_out, State26_out, State24_out, State22_out, State20_out, State18_out, State16_out, State14_out, State12_out, State10_out, State8_out, State6_out, State4_out, InstrRegEN);
  or or_23 (PCEN, State34_out, State35_out, out_13[2], InstrRegEN);
  or or_24 (out_18, State3_out, out_4, State34_out, State35_out, out_13[2], State38_out, State37_out);
  or or_25 (out_19[1], State38_out, State37_out);
  or or_26 (out_19[0], out_19[2], State38_out, State3_out);
  or or_27 (NS0, InstrRegEN, and_37_out, and_4_out, and_6_out, and_8_out, and_11_out, and_38_out, and_13_out, and_15_out, and_17_out, and_19_out, and_36_out, and_20_out, and_23_out, and_25_out, and_27_out, and_29_out, and_31_out, and_33_out);
  or or_28 (NS1, and_37_out, and_35_out, and_32_out, and_29_out, and_26_out, and_25_out, and_22_out, and_19_out, and_20_out, and_16_out, and_15_out, and_12_out, and_11_out, and_6_out, and_3_out, and_7_out, and_31_out, and_30_out, and_2_out);
  or or_29 (NS2, and_34_out, and_33_out, and_32_out, and_29_out, and_24_out, and_23_out, and_22_out, and_21_out, and_20_out, and_19_out, and_14_out, and_13_out, and_12_out, and_11_out, and_38_out, and_5_out, and_4_out, and_3_out, and_2_out);
  or or_30 (NS3, and_28_out, and_27_out, and_26_out, and_25_out, and_24_out, and_23_out, and_22_out, and_20_out, and_19_out, and_10_out, and_8_out, and_7_out, and_6_out, and_5_out, and_4_out, and_3_out);
  or or_31 (NS4, and_20_out, and_18_out, and_17_out, and_16_out, and_15_out, and_14_out, and_13_out, and_12_out, and_11_out, and_10_out, and_8_out, and_7_out, and_6_out, and_5_out, and_4_out, and_3_out);
  and and_39 (and_39_out, in_2[0], in_2[1], in_2[2], in_2[3], in_2[4], in_2[5], in_2[6], in_2[7], in_2[8], in_2[9], in_2[10], in_2[11], in_2[12], in_2[13], in_2[14], in_2[15], in_2[16], in_2[17], in_2[18], in_2[19], in_2[20], in_2[21], in_2[22], in_2[23], in_2[24], in_2[25], in_2[26], in_2[27], in_2[28], in_2[29], in_2[30], in_2[31]);
  or or_32 (NS5, and_2_out, and_31_out, and_30_out, and_21_out, and_36_out, and_38_out, and_9_out);

  assign out_13[1] = ALUOpA;
  assign out_17 = out_5;
  assign PCSrc = out_19[2];

  // Notes on the sheet:
  //   NextState1
  //   NextState3
  //   NextState0 unused
  //   NextState38
  //   ALUCtrl2
  //   ALUCtrl1
  //   ALUCtrl0
  //   CompUnitsOpB2
  //   CompUnitsOpB1
  //   CompUnitsOpB0
  //   NextState30
  //   NextState29
  //   NextState28
  //   NextState27
  //   NextState26
  //   NextState25
  //   NextState32
  //   NextState24
  //   NextState23
  //   NextState37
  //   NextState22
  //   NextState21
  //   NextState20
  //   NextState19
  //   NextState18
  //   NextState17
  //   NextState16
  //   NextState15
  //   NextState33
  //   NextState31
  //   NextState14
  //   NextState13
  //   SHIFTCtrl1
  //   SHIFTCtrl0
  //   SHIFTOpB1
  //   SHIFTOpB0
  //   ReadAddrBorC
  //   WriteRegEN
  //   WriteDataSrc2
  //   WriteDataSrc1
  //   WriteDataSrc0
  //   NextState36
  //   NextState12
  //   NextState11
  //   NextState10
  //   NextState9
  //   NextState8
  //   NextState7
  //   NextState34
  //   NextState35
  //   NextState6
  //   NextState5
  //   NextState4
  //   NextState2
  //   LoadDataOutMemEN
  //   WriteDataInMemEN
  //   CompUnitsOpB
  //   WriteDataSrc
  //   Branch
endmodule
